# Fritzing sketch Laser Tripwire Sketch (saved by Fritzing 0.9.3b)
breadboards: 1

parts:
  Part1 = Arduino Uno (Rev3)
  R1 = PHOTOCELL [package=photocell-kit]
  R2 = Resistor [tolerance=±5% resistance=330 package="0402 [SMD]"]

nets:
  N1: Part1.A0, R1.P$1, R2.Pin_1
  N2: Part1.5V, R1.P$2
  N3: Part1.GND, R2.Pin_0

notes:
  VCC (TMC1638)
  GND (TMC1638)
  STB (TMC1638)
  CLK (TMC1638)
  DIO (TMC1638)
  +5V (Laser)
  GND (Laser)
